# Fritzing sketch circuit_schema (saved by Fritzing 0.9.4)

parts:
  Part1 = Arduino Uno (Rev3)
  8_Channel_Relay1 = 8 Channel Power Relay
  M1 = DC Motor
  M2 = DC Motor
  S1 = Toggle Switch [package=THT]
  S2 = Toggle Switch [package=THT]
  Mod1 = flyskyr6b_1
  M3 = RioRand LM2596
  JACK2 = 2.1mm Barrel Jack with Terminal Block
  BAT2 = 12 battery [package=battery]

nets:
  N1: Part1.D8, 8_Channel_Relay1.IN6
  N2: Part1.D9_PWM, 8_Channel_Relay1.IN5
  N3: Part1.D10_PWM/SS, 8_Channel_Relay1.IN4
  N4: Part1.D11_PWM/MOSI, 8_Channel_Relay1.IN3
  N5: Part1.D12/MISO, 8_Channel_Relay1.IN2
  N6: Part1.D13/SCK, 8_Channel_Relay1.IN1
  N7: Part1.D2, Mod1.connector2
  N8: Part1.D3_PWM, Mod1.connector0
  N9: Part1.D4, Mod1.connector1
  N10: Part1.D5_PWM, Mod1.connector4
  N11: Part1.D6_PWM, 8_Channel_Relay1.IN8
  N12: Part1.D7, 8_Channel_Relay1.IN7
  3V3: Part1.3V3, 8_Channel_Relay1.VCC
  N13: Part1.5V, Mod1.connector13
  GND: Part1.GND, 8_Channel_Relay1.GND, Mod1.connector20
  N14: 8_Channel_Relay1.NC#21, S1.L1
  N15: 8_Channel_Relay1.COM#22, 8_Channel_Relay1.COM#25, S1.COM
  N16: 8_Channel_Relay1.NC#24, S1.L2
  N17: 8_Channel_Relay1.NC#27, S2.L1
  N18: 8_Channel_Relay1.COM#28, 8_Channel_Relay1.COM#31, S2.COM
  N19: 8_Channel_Relay1.NC#30, S2.L2
  N20: 8_Channel_Relay1.NC#33, 8_Channel_Relay1.NC#36, 8_Channel_Relay1.NC#39, 8_Channel_Relay1.NC#42, M3.Pin_2, BAT2.-
  N21: 8_Channel_Relay1.COM#34, M2.pin_1
  N22: 8_Channel_Relay1.NO, M3.Pin_1, BAT2.+
  N23: 8_Channel_Relay1.COM#37, M2.pin_2
  N24: 8_Channel_Relay1.COM#40, M1.pin_1
  N25: 8_Channel_Relay1.COM#43, M1.pin_2
  N26: M3.Pin_3, JACK2.POS
  N27: M3.Pin_4, JACK2.NEG

custom parts:
  8 Channel Power Relay: An 8 channel power relay. The module operates at 5V.
  12 battery: 12V lead acid type battery, like the Husqvarna YTH2448 12V 35AH battery. This is the mini version 1/4 the size of the actual battery to be closer to typical breadboard parts (around 2in wide rathher than 7in). The pads in pcb are sized to accomidate up to 14ga wire (as these batterys will deliver high currents.)
